# Fritzing sketch i401 (saved by Fritzing 0.9.2b)
perfboards: 4

parts:
  PIC16F1705 = IC, DIP package, 14 pins [chip_label=PIC]
  C1 = Ceramic Capacitor [capacitance=33pF package="100 mil [THT, multilayer]"]
  C2 = Ceramic Capacitor [capacitance=33pF package="100 mil [THT, multilayer]"]
  S1 = Toggle Switch [package=THT]
  S2 = Pushbutton [package=THT]
  S3 = Pushbutton [package=THT]
  XTAL1 = Crystal [frequency="32 kHz" package=THT]
  SPKR1 = Loudspeaker
  U1 = microSD Socket [package=micro-sd-socket-pp]
  JP1 = Header 5 [package=1x05-1mm-ra]
  R1 = Rotary Potentiometer (Small) [maximum_resistance=1kΩ package=THT]
  VCC = 4 x AAA Battery Mount

nets (from the schematic view):
  N1: PIC16F1705.pin1, S1.COM, U1.VCC, JP1.2
  N2: PIC16F1705.pin2, C1.1, XTAL1.pin_1
  N3: PIC16F1705.pin3, C2.1, XTAL1.pin_0
  N4: PIC16F1705.pin4, JP1.1
  N5: PIC16F1705.pin5, S2.leg0
  N6: PIC16F1705.pin6, U1.DI
  N7: PIC16F1705.pin7, U1.CS
  N8: PIC16F1705.pin8, SPKR1.pin1
  N9: PIC16F1705.pin9, U1.DO
  N10: PIC16F1705.pin10, U1.SCK
  N11: PIC16F1705.pin11, S3.leg0
  N12: PIC16F1705.pin12, JP1.5
  N13: PIC16F1705.pin13, JP1.4
  N14: PIC16F1705.pin14, C1.0, C2.0, S2.leg1, S3.leg1, U1.GND, JP1.3, R1.leg2, VCC.-
  N15: S1.L2, VCC.+
  N16: SPKR1.pin2, R1.wiper
